# Fritzing sketch p5-sorting-machine (saved by Fritzing 0.9.3b)
circuit board: 8.46667cm x 5.64444cm
breadboards: 1

parts:
  Part1 = Arduino Mega 2560 (Rev3)
  M2 = Stepper Motor - Unipolar
  M3 = Stepper Motor - Unipolar
  Q1 = Basic FET P-Channel [package="DPak [SMD]"]
  U1 = L298 [package=multiwatt15]
  M1 = Stepper Motor - Unipolar
  J4 = Camdenboss CTB0158-6 [part_number=CTB0158-6 package=THT]
  J5 = Camdenboss CTB0158-6 [part_number=CTB0158-6 package=THT]
  J6 = Camdenboss CTB0158-6 [part_number=CTB0158-6 package=THT]
  Q2 = Basic FET P-Channel [package="DPak [SMD]"]
  Grove2 = Grove Light Sensor
  LED1 = LED - 3mm [color="Red (633nm)" package="3 mm [THT]"]

nets (from the breadboard view):
  N1: Part1.D21/SCL, Grove2.NC
  N2: Part1.D20/SDA, Grove2.SIG
  N3: Part1.D18/TX1, J4.pin5
  3V3: Part1.3V3, Grove2.VCC
  N4: Part1.5V, Q1.drain, U1.VS, U1.IN1, U1.VLS, U1.ENB, J4.pin4, J5.pin4, Q2.drain
  GND: Part1.GND, U1.GND, U1.CSB, J4.pin1, J4.pin3, J5.pin1, J5.pin3, Grove2.GND, LED1.anode
  N5: Part1.D2_PWM, J5.pin5
  N6: Part1.D3_PWM, J6.pin5
  N7: Part1.D23, U1.IN3
  N8: Part1.D25, U1.IN4
  N9: Part1.D27, Q1.Gate
  N10: Part1.D29, Q2.Gate
  N11: Part1.D44, LED1.cathode
  N12: Part1.D47, J5.pin6
  N13: Part1.D49, J4.pin6
  N14: Part1.D51, J6.pin6
  N15: M2.A, J5.terminal_1
  N16: M2.COMMON_1, J5.terminal_2
  N17: M2.C, J5.terminal_3
  N18: M2.B, J5.terminal_4
  N19: M2.COMMON_2, J5.terminal_5
  N20: M2.D, J5.terminal_6
  N21: M3.A, J4.terminal_1
  N22: M3.COMMON_1, J4.terminal_2
  N23: M3.C, J4.terminal_3
  N24: M3.B, J4.terminal_4
  N25: M3.COMMON_2, J4.terminal_5
  N26: M3.D, J4.terminal_6
  N27: Q1.source, J5.pin2
  N28: U1.OUT3, J6.pin2
  N29: U1.OUT4, J6.pin1
  N30: M1.A, J6.terminal_1
  N31: M1.COMMON_1, J6.terminal_2
  N32: M1.C, J6.terminal_3
  N33: M1.B, J6.terminal_4
  N34: M1.COMMON_2, J6.terminal_5
  N35: M1.D, J6.terminal_6
  N36: J4.pin2, Q2.source

custom parts:
  Grove Light Sensor: An analog light sensor
